# Fritzing sketch sensor-breadboard (saved by Fritzing 0.9.3b)
breadboards: 1

parts:
  Part1 = Arduino Pro Mini (3.3V)  # not connected
  Part2 = RFM69 Breakout (915MHz) [part_number=WRL-12775]
  J1 = male pin header, 12 pins [form="♂ (male)"]
  J2 = male pin header, 12 pins [form="♂ (male)"]
  J3 = male pin header, 8 pins [form="♂ (male)"]
  J4 = male pin header, 3 pins [form="♂ (male)"]
  J5 = Screw terminal - 2 pins [package=THT]
  J6 = male pin header, 1 pin [form="♂ (male)"]

nets:
  N1: Part2.MISO, J2.pin3, J3.pin1
  N2: Part2.MOSI, J2.pin2, J3.pin2
  N3: Part2.SCK, J2.pin4, J3.pin3
  N4: Part2.NSS, J2.pin1, J3.pin4
  N5: Part2.RESET, J3.pin5
  N6: Part2.DIO0, J1.pin8, J3.pin6
  N7: Part2.GND, J2.pin11, J3.pin7, J4.pin3, J5.pin2
  N8: Part2.3.3V, J2.pin9, J3.pin8, J4.pin2
  N9: Part2.ANT, J6.pin1
  N10: J2.pin7, J4.pin1
  N11: J2.pin12, J5.pin1

custom parts:
  RFM69 Breakout (915MHz): The RFM69HCW is an inexpensive and versatile radio module. You can use it to send text or binary data between two or hundreds of modules. It’s perfect for building inexpensive short-range wireless networks for home automation, citizen science, and more.
