# Fritzing sketch sensor-pcb (saved by Fritzing 0.9.3b)
circuit board: 3.75cm x 4.25cm
breadboards: 1

parts:
  J1 = female pin header, 8 pins [form="♀ (female)"]
  J4 = female pin header, 12 pins [form="♀ (female)"]
  J10 = Screw terminal - 2 pins [package=THT]
  J2 = female pin header, 8 pins [form="♀ (female)"]
  J11 = female pin header, 1 pin [form="♀ (female)"]
  J5 = female pin header, 12 pins [form="♀ (female)"]
  J6 = female pin header, 3 pins [form="♀ (female)"]

nets:
  N1: J1.pin1, J5.pin10
  N2: J1.pin2, J5.pin11
  N3: J1.pin3, J5.pin9
  N4: J1.pin4, J5.pin12
  N5: J1.pin6, J4.pin5
  N6: J1.pin7, J10.pin1, J5.pin2, J6.pin3
  N7: J1.pin8, J5.pin4, J6.pin2
  N8: J10.pin2, J5.pin1
  N9: J2.pin7, J11.pin1
  N10: J5.pin7, J6.pin1
