# Fritzing sketch sensor-schematic (saved by Fritzing 0.9.3b)
breadboards: 1

parts:
  Part2 = Arduino Pro Mini (3.3V)
  Part1 = RFM69 Breakout (915MHz) [part_number=WRL-12775]
  SENS = male pin header, 3 pins [form="♂ (male)"]
  ANT = male pin header, 1 pin [form="♂ (male)"]
  BAT = Screw terminal - 2 pins [package=THT]

nets:
  VCC: Part2.VCC, Part1.3.3V, SENS.pin2
  N1: Part2.RAW, BAT.pin1
  N2: Part2.A2, SENS.pin1
  N3: Part2.SCK, Part1.SCK
  N4: Part2.MISO, Part1.MISO
  N5: Part2.MOSI, Part1.MOSI
  N6: Part2.D10, Part1.NSS
  N7: Part2.D2, Part1.DIO0
  GND: Part2.GND, Part1.GND, SENS.pin3, BAT.pin2
  N8: Part1.ANT, ANT.pin1

custom parts:
  RFM69 Breakout (915MHz): The RFM69HCW is an inexpensive and versatile radio module. You can use it to send text or binary data between two or hundreds of modules. It’s perfect for building inexpensive short-range wireless networks for home automation, citizen science, and more.
