# Fritzing sketch soil-moisture-sensor-pcb (saved by Fritzing 0.9.3b)
circuit board: 3.33cm x 3.33cm
breadboards: 1

parts:
  J1 = female pin header, 8 pins [form="♀ (female)"]
  J3 = female pin header, 12 pins [form="♀ (female)"]
  J4 = female pin header, 12 pins [form="♀ (female)"]
  J5 = female pin header, 8 pins [form="♀ (female)"]
  J6 = female pin header, 3 pins [form="♀ (female)"]
  J7 = female pin header, 1 pin [form="♀ (female)"]

nets:
  N1: J1.pin1, J3.pin10
  N2: J1.pin2, J3.pin11
  N3: J1.pin3, J3.pin9
  N4: J1.pin4, J3.pin12
  N5: J1.pin6, J4.pin5
  N6: J1.pin7, J3.pin2
  N7: J1.pin8, J3.pin4, J6.pin2
  N8: J3.pin7, J6.pin3
  N9: J4.pin4, J6.pin1
  N10: J5.pin7, J7.pin1
