# Fritzing sketch Soil Moisture Sensor Schematic (saved by Fritzing 0.9.3b)
breadboards: 1

parts:
  Part2 = Arduino Pro Mini (3.3V)
  Part1 = RFM69 Breakout (915MHz) [part_number=WRL-12775]
  ANT = Header 1 [package=1x01_offset]
  SENS = Header 1 [package=1x01_offset]
  JP3 = Header 1 [package=1x01_offset]
  JP2 = Header 1 [package=1x01_offset]

nets:
  VCC: Part2.VCC, Part1.3.3V, JP3.1
  N1: Part2.A1, SENS.1
  N2: Part2.SCK, Part1.SCK
  N3: Part2.MISO, Part1.MISO
  N4: Part2.MOSI, Part1.MOSI
  N5: Part2.D10, Part1.NSS
  N6: Part2.D2, Part1.DIO0
  GND: Part2.GND, Part1.GND, JP2.1
  N7: Part1.ANT, ANT.1

custom parts:
  RFM69 Breakout (915MHz): The RFM69HCW is an inexpensive and versatile radio module. You can use it to send text or binary data between two or hundreds of modules. It’s perfect for building inexpensive short-range wireless networks for home automation, citizen science, and more.
